# Fritzing sketch Wireing (saved by Fritzing 0.9.3b)

parts:
  LilyGo_T-Display_S3_(ESP32_+_1_9"_8Bit_LCD_Screen) = lilygo t-display-S3
  M1 = Niren can bus module [package=THT]
  OBD2_Stecker = shrouded pin header, 16 pins [form="♂ (shrouded male)"]

nets:
  N1: LilyGo_T-Display_S3_(ESP32_+_1_9"_8Bit_LCD_Screen).Pin_17, M1.pin1
  N2: LilyGo_T-Display_S3_(ESP32_+_1_9"_8Bit_LCD_Screen).Pin_18, M1.pin2
  N3: LilyGo_T-Display_S3_(ESP32_+_1_9"_8Bit_LCD_Screen).Pin_20, LilyGo_T-Display_S3_(ESP32_+_1_9"_8Bit_LCD_Screen).Pin_21, M1.pin3
  N4: LilyGo_T-Display_S3_(ESP32_+_1_9"_8Bit_LCD_Screen).Pin_22, M1.pin4
  N5: LilyGo_T-Display_S3_(ESP32_+_1_9"_8Bit_LCD_Screen).Pin_23, M1.pin5
  N6: LilyGo_T-Display_S3_(ESP32_+_1_9"_8Bit_LCD_Screen).Pin_24, M1.pin6
  N7: LilyGo_T-Display_S3_(ESP32_+_1_9"_8Bit_LCD_Screen).Pin_25, M1.pin7
  N8: M1.pin10, M1.pin12, OBD2_Stecker.pin6
  N9: M1.pin11, M1.pin13, OBD2_Stecker.pin11

notes:
  Pin 6 CAN High
  Pin 14 CAN Low

custom parts:
  lilygo t-display-S3: T-Display-S3 ESP32-S3 1.9 inch ST7789 LCD Display Development Board WIFI Bluetooth5.0 Wireless Module 170*320 Resolution.
  Niren can bus module: Niren can bus module availabe on ebay and others. Pcb view assumes that you unsolder the 7 pin header and resolder it on the bottom of the module to connect to the pcb. The two jumpers and the can bus connector remain on the top of the board and don't appear in pcb view.
