# Fritzing sketch HWv2 wireing (saved by Fritzing 0.9.3b)

parts:
  NodeMCU_Dev_Kit_v1 = DOIT Esp32 DevKit v1 (30 pins long, 11 pins width) [part_number=ESP32S-PIN30]
  1_28"_TFT_GC9A01_240x240px = GC9A01 round lcd
  CAN_Bus_Module = Niren can bus module [package=THT]
  LM2596S_DC-DC_Step_Down_Module = LM2596 step down module
  OBDII = OBD2

nets:
  N1: NodeMCU_Dev_Kit_v1.3V3, 1_28"_TFT_GC9A01_240x240px.Pin_7, CAN_Bus_Module.pin1
  N2: NodeMCU_Dev_Kit_v1.GND, 1_28"_TFT_GC9A01_240x240px.Pin_6, CAN_Bus_Module.pin2, LM2596S_DC-DC_Step_Down_Module.IN-, LM2596S_DC-DC_Step_Down_Module.OUT-, OBDII.pin_4
  N3: NodeMCU_Dev_Kit_v1.D15, CAN_Bus_Module.pin3
  N4: NodeMCU_Dev_Kit_v1.D4, 1_28"_TFT_GC9A01_240x240px.Pin_1
  N5: NodeMCU_Dev_Kit_v1.D5, 1_28"_TFT_GC9A01_240x240px.Pin_2
  N6: NodeMCU_Dev_Kit_v1.D19, 1_28"_TFT_GC9A01_240x240px.Pin_3
  N7: NodeMCU_Dev_Kit_v1.D22, 1_28"_TFT_GC9A01_240x240px.Pin_5
  N8: NodeMCU_Dev_Kit_v1.D23, 1_28"_TFT_GC9A01_240x240px.Pin_4
  N9: NodeMCU_Dev_Kit_v1.D27, CAN_Bus_Module.pin7
  N10: NodeMCU_Dev_Kit_v1.D14, CAN_Bus_Module.pin6
  N11: NodeMCU_Dev_Kit_v1.D12, CAN_Bus_Module.pin4
  N12: NodeMCU_Dev_Kit_v1.D13, CAN_Bus_Module.pin5
  N13: NodeMCU_Dev_Kit_v1.VIN, LM2596S_DC-DC_Step_Down_Module.OUT+
  N14: CAN_Bus_Module.pin10, CAN_Bus_Module.pin12, OBDII.pin_14
  N15: CAN_Bus_Module.pin11, CAN_Bus_Module.pin13, OBDII.pin_6
  N16: LM2596S_DC-DC_Step_Down_Module.IN+, OBDII.pin_16

custom parts:
  DOIT Esp32 DevKit v1 (30 pins long, 11 pins width): The DOIT Esp32 DevKit v1 is one of the development board created by DOIT to evaluate the ESP-WROOM-32 module. It is based on the ESP32 microcontroller that boasts Wifi, Bluetooth, Ethernet and Low Power support all in a single chip. (vanepp) made breadboard work, adjusted pin numbering and labels and reduced size of schematic and cleaned up pcb. This chip is 30pins long (2 x15) and 11 pins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
  GC9A01 round lcd: IPS TFT display round 1.28″ 240×240 GC9A01 controller. Mar 2025 fix pcb pin with fill #ffffff instead of none. Casuses problem in etchable pcb images (pad with no hole.)
  Niren can bus module: Niren can bus module availabe on ebay and others. Pcb view assumes that you unsolder the 7 pin header and resolder it on the bottom of the module to connect to the pcb. The two jumpers and the can bus connector remain on the top of the board and don't appear in pcb view.
  LM2596 step down module: LM2596 DC-DC step down power supply module 3 A.
